// Logisim project bancore.circ as structural Verilog: 23 circuits, main circuit main
module main (
  input  [7:0] Insere_Valor,
  input  Sel_Valor,
  input  [1:0] W,
  input  [1:0] A,
  input  [1:0] B,
  input  Escreve,
  input  [2:0] SelOp3,
  output z,
  output [7:0] S,
  output c
);

  wire [7:0] banco_de_registradores_1_a, banco_de_registradores_1_b, mux_2por1_8_1_vw;

  LED led_1 (.in(S[0]));
  LED led_2 (.in(S[1]));
  LED led_3 (.in(S[2]));
  LED led_4 (.in(S[3]));
  LED led_5 (.in(S[4]));
  LED led_6 (.in(S[5]));
  LED led_7 (.in(S[6]));
  LED led_8 (.in(S[7]));
  banco_de_registradores banco_de_registradores_1 (
    .escreve(Escreve), .VW(mux_2por1_8_1_vw), .Sel_RW(W), .RB(A), .RA(B), .B(banco_de_registradores_1_b),
    .A(banco_de_registradores_1_a));
  LED LED_saiu0 (.in(z));
  LED LED_over_underflow (.in(c));
  ULA ula_1 (.SelOp_3(SelOp3), .B(banco_de_registradores_1_b), .A(banco_de_registradores_1_a), .Z(z), .S(S), .C(c));
  mux_2por1_8 mux_2por1_8_1 (.S(S), .In_valor(Insere_Valor), .Sel_valor(Sel_Valor), .VW(mux_2por1_8_1_vw));
endmodule

module regist_8 (
  input  [7:0] entrada,
  input  escreve,
  output [7:0] saida
);

  wire undriven;

  D_Flip_Flop d_ff_1 (.D(entrada[0]), .clk(escreve), .Q(saida[0]), .preset(undriven));  // open: Qn, reset
  D_Flip_Flop d_ff_2 (.D(entrada[1]), .clk(escreve), .Q(saida[1]));  // open: Qn, preset, reset
  D_Flip_Flop d_ff_3 (.D(entrada[2]), .clk(escreve), .Q(saida[2]));  // open: Qn, preset, reset
  D_Flip_Flop d_ff_4 (.D(entrada[3]), .clk(escreve), .Q(saida[3]));  // open: Qn, preset, reset
  D_Flip_Flop d_ff_5 (.D(entrada[4]), .clk(escreve), .Q(saida[4]));  // open: Qn, preset, reset
  D_Flip_Flop d_ff_6 (.D(entrada[5]), .clk(escreve), .Q(saida[5]));  // open: Qn, preset, reset
  D_Flip_Flop d_ff_7 (.D(entrada[6]), .clk(escreve), .Q(saida[6]));  // open: Qn, preset, reset
  D_Flip_Flop d_ff_8 (.D(entrada[7]), .clk(escreve), .Q(saida[7]));  // open: Qn, preset, reset
endmodule

module banco_de_registradores (
  input  [1:0] RB,
  input  [1:0] RA,
  input  escreve,
  input  [1:0] Sel_RW,
  input  [7:0] VW,
  output [7:0] B,
  output [7:0] A
);

  wire demux_4por1_1_1_r0, demux_4por1_1_1_r1, demux_4por1_1_1_r2, demux_4por1_1_1_r3;
  wire [7:0] demux_4po1_8_1_r0, demux_4po1_8_1_r1, demux_4po1_8_1_r2, demux_4po1_8_1_r3, regist_8_1_saida,
       regist_8_2_saida, regist_8_3_saida, regist_8_4_saida;

  demux_4po1_8 demux_4po1_8_1 (
    .Sel_RW(Sel_RW), .VW(VW), .R0(demux_4po1_8_1_r0), .R1(demux_4po1_8_1_r1), .R2(demux_4po1_8_1_r2),
    .R3(demux_4po1_8_1_r3));
  demux_4por1_1 demux_4por1_1_1 (
    .S2(Sel_RW[1]), .S1(Sel_RW[0]), .E(escreve), .R0(demux_4por1_1_1_r0), .R1(demux_4por1_1_1_r1),
    .R2(demux_4por1_1_1_r2), .R3(demux_4por1_1_1_r3));
  regist_8 regist_8_1 (.entrada(demux_4po1_8_1_r0), .escreve(demux_4por1_1_1_r0), .saida(regist_8_1_saida));
  regist_8 regist_8_2 (.entrada(demux_4po1_8_1_r1), .escreve(demux_4por1_1_1_r1), .saida(regist_8_2_saida));
  regist_8 regist_8_3 (.entrada(demux_4po1_8_1_r2), .escreve(demux_4por1_1_1_r2), .saida(regist_8_3_saida));
  regist_8 regist_8_4 (.entrada(demux_4po1_8_1_r3), .escreve(demux_4por1_1_1_r3), .saida(regist_8_4_saida));
  mux_4por1_8 mux_4por1_8_1 (
    .R1(regist_8_2_saida), .R2(regist_8_3_saida), .R3(regist_8_4_saida), .R(RB), .R0(regist_8_1_saida), .AB(B));
  mux_4por1_8 mux_4por1_8_2 (
    .R1(regist_8_2_saida), .R2(regist_8_3_saida), .R3(regist_8_4_saida), .R(RA), .R0(regist_8_1_saida), .AB(A));
endmodule

module mux_2por1_1 (
  input  Sel_valor,
  input  Insere,
  input  S,
  output VW
);

  wire and_1_out, and_2_out, not_1_out;

  not not_1 (not_1_out, Sel_valor);
  and and_1 (and_1_out, Insere, Sel_valor);
  and and_2 (and_2_out, S, not_1_out);
  or or_1 (VW, and_1_out, and_2_out);
endmodule

module mux_2por1_8 (
  input  [7:0] S,
  input  [7:0] In_valor,
  input  Sel_valor,
  output [7:0] VW
);

  mux_2por1_1 mux_2por1_1_1 (.Insere(In_valor[0]), .Sel_valor(Sel_valor), .S(S[0]), .VW(VW[0]));
  mux_2por1_1 mux_2por1_1_2 (.Insere(In_valor[1]), .Sel_valor(Sel_valor), .S(S[1]), .VW(VW[1]));
  mux_2por1_1 mux_2por1_1_3 (.Insere(In_valor[2]), .Sel_valor(Sel_valor), .S(S[2]), .VW(VW[2]));
  mux_2por1_1 mux_2por1_1_4 (.Insere(In_valor[3]), .Sel_valor(Sel_valor), .S(S[3]), .VW(VW[3]));
  mux_2por1_1 mux_2por1_1_5 (.Insere(In_valor[4]), .Sel_valor(Sel_valor), .S(S[4]), .VW(VW[4]));
  mux_2por1_1 mux_2por1_1_6 (.Insere(In_valor[5]), .Sel_valor(Sel_valor), .S(S[5]), .VW(VW[5]));
  mux_2por1_1 mux_2por1_1_7 (.Insere(In_valor[6]), .Sel_valor(Sel_valor), .S(S[6]), .VW(VW[6]));
  mux_2por1_1 mux_2por1_1_8 (.Insere(In_valor[7]), .Sel_valor(Sel_valor), .S(S[7]), .VW(VW[7]));
endmodule

module mux_3por1_1 (
  input  ENA,
  input  ENB,
  input  ENC,
  input  A,
  input  B,
  input  C,
  output out_7
);

  wire nand_1_out, nand_2_out, nand_3_out;

  nand nand_1 (nand_1_out, A, ENA);
  nand nand_2 (nand_2_out, B, ENB);
  nand nand_3 (nand_3_out, C, ENC);
  nand nand_4 (out_7, nand_1_out, nand_2_out, nand_3_out);
endmodule

module mux_4por1_1 (
  input  S1,
  input  S0,
  input  R0,
  input  R1,
  input  R2,
  input  R3,
  output \bit 
);

  wire and_1_out, and_2_out, and_3_out, and_4_out, not_1_out, not_2_out;

  not not_1 (not_1_out, S1);
  not not_2 (not_2_out, S0);
  and and_1 (and_1_out, not_2_out, not_1_out, R0);
  and and_2 (and_2_out, not_1_out, S0, R1);
  and and_3 (and_3_out, not_2_out, S1, R2);
  and and_4 (and_4_out, S0, S1, R3);
  or or_1 (\bit , and_1_out, and_2_out, and_3_out, and_4_out);
endmodule

// 4x1-8
module mux_4por1_8 (
  input  [1:0] R,
  input  [7:0] R0,
  input  [7:0] R1,
  input  [7:0] R2,
  input  [7:0] R3,
  output [7:0] AB
);

  mux_4por1_1 mux_4por1_1_1 (.R0(R3[7]), .R1(R2[7]), .R2(R1[7]), .R3(R0[7]), .S1(R[1]), .S0(R[0]), .\bit (AB[7]));
  mux_4por1_1 mux_4por1_1_2 (.R0(R3[6]), .R1(R2[6]), .R2(R1[6]), .R3(R0[6]), .S1(R[1]), .S0(R[0]), .\bit (AB[6]));
  mux_4por1_1 mux_4por1_1_3 (.R0(R3[5]), .R1(R2[5]), .R2(R1[5]), .R3(R0[5]), .S1(R[1]), .S0(R[0]), .\bit (AB[5]));
  mux_4por1_1 mux_4por1_1_4 (.R0(R3[4]), .R1(R2[4]), .R2(R1[4]), .R3(R0[4]), .S1(R[1]), .S0(R[0]), .\bit (AB[4]));
  mux_4por1_1 mux_4por1_1_5 (.R0(R3[3]), .R1(R2[3]), .R2(R1[3]), .R3(R0[3]), .S1(R[1]), .S0(R[0]), .\bit (AB[3]));
  mux_4por1_1 mux_4por1_1_6 (.R0(R3[2]), .R1(R2[2]), .R2(R1[2]), .R3(R0[2]), .S1(R[1]), .S0(R[0]), .\bit (AB[2]));
  mux_4por1_1 mux_4por1_1_7 (.R0(R3[1]), .R1(R2[1]), .R2(R1[1]), .R3(R0[1]), .S1(R[1]), .S0(R[0]), .\bit (AB[1]));
  mux_4por1_1 mux_4por1_1_8 (.R0(R3[0]), .R1(R2[0]), .R2(R1[0]), .R3(R0[0]), .S1(R[1]), .S0(R[0]), .\bit (AB[0]));
endmodule

module multiplex1_ULA (
  input  io,
  input  i1,
  input  i2,
  input  i3,
  input  i4,
  input  i5,
  input  i6,
  input  i7,
  input  s0,
  input  s1,
  input  s2,
  output out_12
);

  wire and_1_out, and_2_out, and_3_out, and_4_out, and_5_out, and_6_out, and_7_out, and_8_out, not_1_out,
       not_2_out, not_3_out;

  not not_1 (not_1_out, s0);
  not not_2 (not_2_out, s1);
  not not_3 (not_3_out, s2);
  and and_1 (and_1_out, io, not_1_out, not_2_out, not_3_out);
  and and_2 (and_2_out, i1, not_1_out, not_2_out, not_3_out);
  and and_3 (and_3_out, i2, not_1_out, not_2_out, not_3_out);
  and and_4 (and_4_out, i3, not_1_out, not_2_out, not_3_out);
  and and_5 (and_5_out, i4, not_1_out, not_2_out, not_3_out);
  and and_6 (and_6_out, i5, not_1_out, not_2_out, not_3_out);
  and and_7 (and_7_out, i6, not_1_out, not_2_out, not_3_out);
  and and_8 (and_8_out, i7, not_1_out, not_2_out, not_3_out);
  or or_1 (out_12, and_1_out, and_2_out, and_3_out, and_4_out, and_5_out, and_6_out, and_7_out, and_8_out);
endmodule

module multiplex8_ULA (
  input  [7:0] op_000,
  input  [7:0] op_001,
  input  [7:0] op_010,
  input  [7:0] op_011,
  input  [7:0] op_100,
  input  [7:0] op_101,
  input  [7:0] op_110,
  input  [7:0] op_111,
  input  [2:0] SelOP,
  output [7:0] out_10
);

  multiplex1_ULA multiplex1_ula_1 (
    .io(op_000[0]), .i1(op_001[0]), .i2(op_010[0]), .i3(op_011[0]), .i4(op_100[0]), .i5(op_101[0]),
    .i6(op_110[0]), .i7(op_111[0]), .s0(SelOP[0]), .s1(SelOP[1]), .s2(SelOP[2]), .out_12(out_10[7]));
  multiplex1_ULA multiplex1_ula_2 (
    .io(op_000[1]), .i1(op_001[1]), .i2(op_010[1]), .i3(op_011[1]), .i4(op_100[1]), .i5(op_101[1]),
    .i6(op_110[1]), .i7(op_111[1]), .s0(SelOP[0]), .s1(SelOP[1]), .s2(SelOP[2]), .out_12(out_10[6]));
  multiplex1_ULA multiplex1_ula_3 (
    .io(op_000[2]), .i1(op_001[2]), .i2(op_010[2]), .i3(op_011[2]), .i4(op_100[2]), .i5(op_101[2]),
    .i6(op_110[2]), .i7(op_111[2]), .s0(SelOP[0]), .s1(SelOP[1]), .s2(SelOP[2]), .out_12(out_10[5]));
  multiplex1_ULA multiplex1_ula_4 (
    .io(op_000[3]), .i1(op_001[3]), .i2(op_010[3]), .i3(op_011[3]), .i4(op_100[3]), .i5(op_101[3]),
    .i6(op_110[3]), .i7(op_111[3]), .s0(SelOP[0]), .s1(SelOP[1]), .s2(SelOP[2]), .out_12(out_10[4]));
  multiplex1_ULA multiplex1_ula_5 (
    .io(op_000[4]), .i1(op_001[4]), .i2(op_010[4]), .i3(op_011[4]), .i4(op_100[4]), .i5(op_101[4]),
    .i6(op_110[4]), .i7(op_111[4]), .s0(SelOP[0]), .s1(SelOP[1]), .s2(SelOP[2]), .out_12(out_10[3]));
  multiplex1_ULA multiplex1_ula_6 (
    .io(op_000[5]), .i1(op_001[5]), .i2(op_010[5]), .i3(op_011[5]), .i4(op_100[5]), .i5(op_101[5]),
    .i6(op_110[5]), .i7(op_111[5]), .s0(SelOP[0]), .s1(SelOP[1]), .s2(SelOP[2]), .out_12(out_10[2]));
  multiplex1_ULA multiplex1_ula_7 (
    .io(op_000[6]), .i1(op_001[6]), .i2(op_010[6]), .i3(op_011[6]), .i4(op_100[6]), .i5(op_101[6]),
    .i6(op_110[6]), .i7(op_111[6]), .s0(SelOP[0]), .s1(SelOP[1]), .s2(SelOP[2]), .out_12(out_10[1]));
  multiplex1_ULA multiplex1_ula_8 (
    .io(op_000[7]), .i1(op_001[7]), .i2(op_010[7]), .i3(op_011[7]), .i4(op_100[7]), .i5(op_101[7]),
    .i6(op_110[7]), .i7(op_111[7]), .s0(SelOP[0]), .s1(SelOP[1]), .s2(SelOP[2]), .out_12(out_10[0]));
endmodule

module demux_4por1_1 (
  input  S2,
  input  S1,
  input  E,
  output R0,
  output R1,
  output R2,
  output R3
);

  wire not_1_out, not_2_out, not_3_out, not_4_out;

  not not_1 (not_1_out, S1);
  not not_2 (not_2_out, S2);
  not not_3 (not_3_out, S2);
  not not_4 (not_4_out, S1);
  and and_1 (R0, E, not_1_out, not_2_out);
  and and_2 (R1, E, S1, not_3_out);
  and and_3 (R2, E, not_4_out, S2);
  and and_4 (R3, E, S1, S2);
endmodule

module demux_4po1_8 (
  input  [1:0] Sel_RW,
  input  [7:0] VW,
  output [7:0] R0,
  output [7:0] R1,
  output [7:0] R2,
  output [7:0] R3
);

  demux_4por1_1 demux_4por1_1_1 (
    .S2(Sel_RW[1]), .S1(Sel_RW[0]), .E(VW[7]), .R0(R0[7]), .R1(R1[7]), .R2(R2[7]), .R3(R3[7]));
  demux_4por1_1 demux_4por1_1_2 (
    .S2(Sel_RW[1]), .S1(Sel_RW[0]), .E(VW[6]), .R0(R0[6]), .R1(R1[6]), .R2(R2[6]), .R3(R3[6]));
  demux_4por1_1 demux_4por1_1_3 (
    .S2(Sel_RW[1]), .S1(Sel_RW[0]), .E(VW[5]), .R0(R0[5]), .R1(R1[5]), .R2(R2[5]), .R3(R3[5]));
  demux_4por1_1 demux_4por1_1_4 (
    .S2(Sel_RW[1]), .S1(Sel_RW[0]), .E(VW[4]), .R0(R0[4]), .R1(R1[4]), .R2(R2[4]), .R3(R3[4]));
  demux_4por1_1 demux_4por1_1_5 (
    .S2(Sel_RW[1]), .S1(Sel_RW[0]), .E(VW[3]), .R0(R0[3]), .R1(R1[3]), .R2(R2[3]), .R3(R3[3]));
  demux_4por1_1 demux_4por1_1_6 (
    .S2(Sel_RW[1]), .S1(Sel_RW[0]), .E(VW[2]), .R0(R0[2]), .R1(R1[2]), .R2(R2[2]), .R3(R3[2]));
  demux_4por1_1 demux_4por1_1_7 (
    .S2(Sel_RW[1]), .S1(Sel_RW[0]), .E(VW[1]), .R0(R0[1]), .R1(R1[1]), .R2(R2[1]), .R3(R3[1]));
  demux_4por1_1 demux_4por1_1_8 (
    .S2(Sel_RW[1]), .S1(Sel_RW[0]), .E(VW[0]), .R0(R0[0]), .R1(R1[0]), .R2(R2[0]), .R3(R3[0]));
endmodule

module divisao (
  input  [7:0] A,
  input  [7:0] B,
  output [7:0] resultado_divisao,
  output overflow
);

  wire [7:0] divider_1_rem;

  Divider divider_1 (.a(A), .b(B), .out(resultado_divisao), .upper({8{1'b0}}), .rem(divider_1_rem));
  or or_1 (overflow, divider_1_rem[0], divider_1_rem[1], divider_1_rem[2], divider_1_rem[3], divider_1_rem[4], divider_1_rem[5], divider_1_rem[6], divider_1_rem[7]);
endmodule

module a_nor_b (
  input  [7:0] A,
  input  [7:0] B,
  output [7:0] resultado_nor
);

  nor nor_1 (resultado_nor[0], A[0], B[0]);
  nor nor_2 (resultado_nor[1], A[1], B[1]);
  nor nor_3 (resultado_nor[2], A[2], B[2]);
  nor nor_4 (resultado_nor[3], A[3], B[3]);
  nor nor_5 (resultado_nor[4], A[4], B[4]);
  nor nor_6 (resultado_nor[5], A[5], B[5]);
  nor nor_7 (resultado_nor[6], A[6], B[6]);
  nor nor_8 (resultado_nor[7], A[7], B[7]);
endmodule

module a_xor_b (
  input  [7:0] A,
  input  [7:0] B,
  output [7:0] resultado_xor
);

  xor xor_1 (resultado_xor[0], A[0], B[0]);
  xor xor_2 (resultado_xor[1], A[1], B[1]);
  xor xor_3 (resultado_xor[2], A[2], B[2]);
  xor xor_4 (resultado_xor[3], A[3], B[3]);
  xor xor_5 (resultado_xor[4], A[4], B[4]);
  xor xor_6 (resultado_xor[5], A[5], B[5]);
  xor xor_7 (resultado_xor[6], A[6], B[6]);
  xor xor_8 (resultado_xor[7], A[7], B[7]);
endmodule

module multiplicacao (
  input  [7:0] A,
  input  [7:0] B,
  output [7:0] resultado_mult,
  output overflow
);

  wire [7:0] multiplier_1_cout;

  Multiplier multiplier_1 (.a(A), .b(B), .out(resultado_mult), .cin({8{1'b0}}), .cout(multiplier_1_cout));
  or or_1 (overflow, multiplier_1_cout[0], multiplier_1_cout[1], multiplier_1_cout[2], multiplier_1_cout[3], multiplier_1_cout[4], multiplier_1_cout[5], multiplier_1_cout[6], multiplier_1_cout[7]);
endmodule

module adicao_1 (
  input  A,
  input  B,
  input  c,
  output S,
  output ci
);

  wire and_1_out, and_2_out, and_3_out, xor_1_out;

  and and_1 (and_1_out, B, c);
  and and_2 (and_2_out, A, c);
  or or_1 (ci, and_1_out, and_2_out, and_3_out);
  and and_3 (and_3_out, A, B);
  xor xor_1 (xor_1_out, A, B);
  xor xor_2 (S, c, xor_1_out);
endmodule

module subtr_completa (
  input  [7:0] A,
  input  [7:0] B,
  output Over,
  output [7:0] resultado_sub
);

  wire not_1_out, not_2_out, not_3_out, not_4_out, not_5_out, not_6_out, not_7_out, not_8_out,
       subtracao_1_1_c, subtracao_1_1_ci, subtracao_1_2_ci, subtracao_1_3_ci, subtracao_1_4_ci,
       subtracao_1_5_ci, subtracao_1_6_ci, subtracao_1_8_c, subtracao_1_8_ci;

  not not_1 (not_1_out, B[7]);
  subtracao_1 subtracao_1_1 (.A(A[7]), .B(not_1_out), .C(subtracao_1_1_c), .CI(subtracao_1_1_ci), .S(resultado_sub[7]));
  not not_2 (not_2_out, B[6]);
  subtracao_1 subtracao_1_2 (
    .A(A[6]), .B(not_2_out), .C(subtracao_1_1_ci), .CI(subtracao_1_2_ci), .S(resultado_sub[6]));
  not not_3 (not_3_out, B[5]);
  subtracao_1 subtracao_1_3 (
    .A(A[5]), .B(not_3_out), .C(subtracao_1_2_ci), .CI(subtracao_1_3_ci), .S(resultado_sub[5]));
  not not_4 (not_4_out, B[4]);
  subtracao_1 subtracao_1_4 (
    .A(A[4]), .B(not_4_out), .C(subtracao_1_3_ci), .CI(subtracao_1_4_ci), .S(resultado_sub[4]));
  not not_5 (not_5_out, B[3]);
  subtracao_1 subtracao_1_5 (
    .A(A[3]), .B(not_5_out), .C(subtracao_1_4_ci), .CI(subtracao_1_5_ci), .S(resultado_sub[3]));
  not not_6 (not_6_out, B[2]);
  subtracao_1 subtracao_1_6 (
    .A(A[2]), .B(not_6_out), .C(subtracao_1_5_ci), .CI(subtracao_1_6_ci), .S(resultado_sub[2]));
  not not_7 (not_7_out, B[1]);
  subtracao_1 subtracao_1_7 (.A(A[1]), .B(not_7_out), .S(resultado_sub[1]));  // open: C, CI
  not not_8 (not_8_out, B[0]);
  subtracao_1 subtracao_1_8 (.A(A[0]), .B(not_8_out), .C(subtracao_1_8_c), .CI(subtracao_1_8_ci), .S(resultado_sub[0]));
  xor xor_1 (Over, subtracao_1_8_ci, subtracao_1_8_c);
  // also tied to VCC on the sheet: subtracao_1_1_c
endmodule

module ULA (
  input  [7:0] B,
  input  [7:0] A,
  input  [2:0] SelOp_3,
  output Z,
  output [7:0] S,
  output C
);

  wire SELOP_001_overflow, SELOP_011_overflow, SELOP_110_overflow, SELOP_111_over;
  wire [7:0] SELOP_0000_out, SELOP_001_resultado_mult, SELOP_010_out, SELOP_011_resultado_divisao,
       SELOP_100_resultado_nor, SELOP_101_resultado_xor, SELOP_110_resultado_adicao, SELOP_111_resultado_sub;

  assign SELOP_0000_out = B & A;  // AND_Gate SELOP_0000, 8 bits wide
  multiplicacao SELOP_001 (.A(A), .B(B), .resultado_mult(SELOP_001_resultado_mult), .overflow(SELOP_001_overflow));
  assign SELOP_010_out = B | A;  // OR_Gate SELOP_010, 8 bits wide
  divisao SELOP_011 (.A(A), .B(B), .resultado_divisao(SELOP_011_resultado_divisao), .overflow(SELOP_011_overflow));
  a_nor_b SELOP_100 (.A(A), .B(B), .resultado_nor(SELOP_100_resultado_nor));
  a_xor_b SELOP_101 (.A(A), .B(B), .resultado_xor(SELOP_101_resultado_xor));
  adicao_completa SELOP_110 (
    .A(A), .B(B), .resultado_adicao(SELOP_110_resultado_adicao), .overflow(SELOP_110_overflow));
  subtr_completa SELOP_111 (.A(A), .B(B), .Over(SELOP_111_over), .resultado_sub(SELOP_111_resultado_sub));
  nor nor_1 (Z, S[7], S[6], S[5], S[4], S[3], S[2], S[1], S[0]);
  multiplex8_ULA Selecionador (
    .op_000(SELOP_0000_out), .op_001(SELOP_001_resultado_mult), .op_010(SELOP_010_out),
    .op_011(SELOP_011_resultado_divisao), .op_100(SELOP_100_resultado_nor), .op_101(SELOP_101_resultado_xor),
    .op_110(SELOP_110_resultado_adicao), .op_111(SELOP_111_resultado_sub), .SelOP(SelOp_3), .out_10(S));
  multiplex_over3sel Selecionador_Overflow (
    .SelOP(SelOp_3), .multi_001(SELOP_001_overflow), .subt_111(SELOP_111_over),
    .adicao_110(SELOP_110_overflow), .divisao_011(SELOP_011_overflow), .out_6(C));
endmodule

module multiplex_over3sel (
  input  [2:0] SelOP,
  input  multi_001,
  input  subt_111,
  input  adicao_110,
  input  divisao_011,
  output out_6
);

  wire and_1_out, and_2_out, and_3_out, and_4_out, not_1_out, not_2_out, not_3_out;

  not not_1 (not_1_out, SelOP[0]);
  not not_2 (not_2_out, SelOP[1]);
  not not_3 (not_3_out, SelOP[2]);
  and and_1 (and_1_out, SelOP[2], SelOP[1], not_1_out, divisao_011);
  and and_2 (and_2_out, not_3_out, not_2_out, SelOP[0], subt_111);
  and and_3 (and_3_out, not_3_out, SelOP[1], not_1_out, adicao_110);
  and and_4 (and_4_out, not_3_out, SelOP[0], SelOP[0], multi_001);
  or or_1 (out_6, and_2_out, and_3_out, and_4_out, and_1_out);
endmodule

module adicao_completa (
  input  [7:0] A,
  input  [7:0] B,
  output [7:0] resultado_adicao,
  output overflow
);

  wire adicao_1_1_ci, adicao_1_2_ci, adicao_1_3_ci, adicao_1_4_ci, adicao_1_5_ci, adicao_1_6_ci,
       adicao_1_7_ci, soma2bit_1_ci;

  adicao_1 adicao_1_1 (.A(A[7]), .B(B[7]), .c(adicao_1_2_ci), .S(resultado_adicao[7]), .ci(adicao_1_1_ci));
  xor xor_1 (overflow, adicao_1_1_ci, adicao_1_2_ci);
  adicao_1 adicao_1_2 (.A(A[6]), .B(B[6]), .c(adicao_1_3_ci), .S(resultado_adicao[6]), .ci(adicao_1_2_ci));
  adicao_1 adicao_1_3 (.A(A[5]), .B(B[5]), .c(adicao_1_4_ci), .S(resultado_adicao[5]), .ci(adicao_1_3_ci));
  adicao_1 adicao_1_4 (.A(A[4]), .B(B[4]), .c(adicao_1_5_ci), .S(resultado_adicao[4]), .ci(adicao_1_4_ci));
  adicao_1 adicao_1_5 (.A(A[3]), .B(B[3]), .c(adicao_1_6_ci), .S(resultado_adicao[3]), .ci(adicao_1_5_ci));
  adicao_1 adicao_1_6 (.A(A[2]), .B(B[2]), .c(adicao_1_7_ci), .S(resultado_adicao[2]), .ci(adicao_1_6_ci));
  adicao_1 adicao_1_7 (.A(A[1]), .B(B[1]), .c(soma2bit_1_ci), .S(resultado_adicao[1]), .ci(adicao_1_7_ci));
  soma2bit soma2bit_1 (.A(A[0]), .B(B[0]), .S(resultado_adicao[0]), .CI(soma2bit_1_ci));
endmodule

module subtracao_1 (
  input  A,
  input  B,
  output C,
  output CI,
  output S
);

  wire and_1_out, and_2_out, and_3_out, xor_1_out;

  and and_1 (and_1_out, B, B);
  and and_2 (and_2_out, A, B);
  or or_1 (CI, and_1_out, and_2_out, and_3_out);
  and and_3 (and_3_out, A, B);
  xor xor_1 (xor_1_out, A, B);
  xor xor_2 (S, B, xor_1_out);

  assign C = B;
endmodule

module soma2bit (
  input  A,
  input  B,
  output S,
  output CI
);

  and and_1 (CI, A, B);
  xor xor_1 (S, A, B);
endmodule
